# Fritzing sketch fritzing_garden (saved by Fritzing 0.9.3b)
breadboards: 1

parts:
  RHT1 = Humidity and Temperature Sensor RHT03
  U1 = NodeMCU V1.0
  PART1 = SparkFun Soil Moisture Sensor [part_number=SEN-13322]

nets:
  VCC: RHT1.Vcc, U1.D1, U1.3V3, PART1.VCC
  N1: RHT1.Data-signal, U1.D4
  GND: RHT1.GND_2, U1.GND, PART1.GND
  N2: U1.D0, U1.RST
  N3: U1.A0, PART1.SIG

notes:
  Fio branco: Deep Sleep
  Fio Cinza: Modo Smart Config (Mudar D1 - GND em 3 segundos para D1 - 3.3 V)

custom parts:
  NodeMCU V1.0: ESP8266 based NodeMCU
  SparkFun Soil Moisture Sensor: The SparkFun Soil Moisture Sensor is a simple breakout for measuring the moisture in soil and similar materials.
